// Logisim project P0_L0_CRC.circ as structural Verilog: 2 circuits, main circuit CRC
module CRC (
  input  [7:0] in_1,
  input  [3:0] in_2,
  output [10:0] out_3
);

  wire n4bit_mod2_1_out_3, n4bit_mod2_2_out_3, n4bit_mod2_3_out_3, n4bit_mod2_4_out_3, n4bit_mod2_5_out_3,
       n4bit_mod2_6_out_3, n4bit_mod2_7_out_3, n4bit_mod2_8_out_3;
  wire [2:0] n4bit_mod2_1_out_4, n4bit_mod2_2_out_4, n4bit_mod2_3_out_4, n4bit_mod2_4_out_4,
       n4bit_mod2_5_out_4, n4bit_mod2_6_out_4, n4bit_mod2_7_out_4;

  // Probe on {in_1, 3'b000}
  // Probe on in_1[7:4]
  _4bit_mod2 u_4bit_mod2_1 (.in_1(in_1[7:4]), .in_2(in_2), .out_3(n4bit_mod2_1_out_3), .out_4(n4bit_mod2_1_out_4));
  // Probe on {n4bit_mod2_1_out_4, in_1[3]}
  _4bit_mod2 u_4bit_mod2_2 (
    .in_1({n4bit_mod2_1_out_4, in_1[3]}), .in_2(in_2), .out_3(n4bit_mod2_2_out_3), .out_4(n4bit_mod2_2_out_4));
  // Probe on {n4bit_mod2_2_out_4, in_1[2]}
  _4bit_mod2 u_4bit_mod2_3 (
    .in_1({n4bit_mod2_2_out_4, in_1[2]}), .in_2(in_2), .out_3(n4bit_mod2_3_out_3), .out_4(n4bit_mod2_3_out_4));
  // Probe on {n4bit_mod2_3_out_4, in_1[1]}
  _4bit_mod2 u_4bit_mod2_4 (
    .in_1({n4bit_mod2_3_out_4, in_1[1]}), .in_2(in_2), .out_3(n4bit_mod2_4_out_3), .out_4(n4bit_mod2_4_out_4));
  // Probe on {n4bit_mod2_4_out_4, in_1[0]}
  _4bit_mod2 u_4bit_mod2_5 (
    .in_1({n4bit_mod2_4_out_4, in_1[0]}), .in_2(in_2), .out_3(n4bit_mod2_5_out_3), .out_4(n4bit_mod2_5_out_4));
  // Probe on {n4bit_mod2_5_out_4, 1'b0}
  _4bit_mod2 u_4bit_mod2_6 (
    .in_1({n4bit_mod2_5_out_4, 1'b0}), .in_2(in_2), .out_3(n4bit_mod2_6_out_3), .out_4(n4bit_mod2_6_out_4));
  // Probe on {n4bit_mod2_6_out_4, 1'b0}
  _4bit_mod2 u_4bit_mod2_7 (
    .in_1({n4bit_mod2_6_out_4, 1'b0}), .in_2(in_2), .out_3(n4bit_mod2_7_out_3), .out_4(n4bit_mod2_7_out_4));
  // Probe on {n4bit_mod2_7_out_4, 1'b0}
  _4bit_mod2 u_4bit_mod2_8 (
    .in_1({n4bit_mod2_7_out_4, 1'b0}), .in_2(in_2), .out_3(n4bit_mod2_8_out_3), .out_4(out_3[2:0]));

  assign out_3[10:3] = in_1;

  // Other names for the same wires on the sheet: 原数据帧[7:0] = in_1; 四位除数[3:0] = in_2
endmodule

module _4bit_mod2 (
  input  [3:0] in_1,
  input  [3:0] in_2,
  output out_3,
  output [2:0] out_4
);

  wire not_1_out;
  wire [3:0] xor_1_out;
  wire [3:3] \余数 ;

  assign xor_1_out = in_1 ^ in_2;  // XOR_Gate xor_1, 4 bits wide
  assign {\余数 [3], out_4} = in_1[3] ? xor_1_out : 4'bz;  // Controlled_Buffer controlled_buffer_1
  not not_1 (not_1_out, in_1[3]);
  assign {\余数 [3], out_4} = not_1_out ? in_1 : 4'bz;  // Controlled_Buffer controlled_buffer_2

  assign out_3 = in_1[3];

  // Other names for the same wires on the sheet: 余数[2:0] = out_4; 被除数[3:0] = in_1; 商 = in_1[3]; 除数[3:0] = in_2
endmodule
