// Logisim project P0_L0_FSM.circ as structural Verilog: 3 circuits, main circuit stateRefresh
module stateRefresh (
  input  I2,
  input  I1,
  input  I0,
  input  char1,
  input  char0,
  output O2,
  output O1,
  output O0
);

  wire and_2_out, and_3_out, and_4_out, and_5_out, and_6_out, and_7_out, and_8_out, not_1_out, not_2_out,
       not_3_out, not_4_out, not_5_out, not_6_out, not_7_out, not_8_out, not_9_out, not_10_out, not_11_out,
       not_12_out, not_13_out, not_14_out;

  not not_1 (not_1_out, char0);
  not not_2 (not_2_out, I1);
  not not_3 (not_3_out, char1);
  not not_4 (not_4_out, I1);
  not not_5 (not_5_out, char0);
  not not_6 (not_6_out, I0);
  not not_7 (not_7_out, char0);
  not not_8 (not_8_out, I0);
  not not_9 (not_9_out, char1);
  not not_10 (not_10_out, I1);
  not not_11 (not_11_out, char0);
  not not_12 (not_12_out, I0);
  not not_13 (not_13_out, char0);
  not not_14 (not_14_out, char1);
  and and_1 (O2, I1, I0, not_1_out);
  and and_2 (and_2_out, not_2_out, I0, not_3_out);
  and and_3 (and_3_out, not_4_out, I0, not_5_out);
  and and_4 (and_4_out, I1, not_6_out, not_7_out);
  and and_5 (and_5_out, not_8_out, not_9_out, char0);
  and and_6 (and_6_out, not_10_out, I0, not_11_out);
  and and_7 (and_7_out, I1, not_12_out, not_13_out);
  and and_8 (and_8_out, I1, not_14_out, char0);
  or or_1 (O1, and_2_out, and_3_out, and_4_out);
  or or_2 (O0, and_5_out, and_6_out, and_7_out, and_8_out);
endmodule

module fsm (
  input  reset,
  input  [1:0] In,
  output out_3
);

  wire clock_1_out;
  wire [2:0] multiplexer_1_out, register_1_q, staterefresh_1_o0;

  stateRefresh staterefresh_1 (
    .I2(register_1_q[2]), .I1(register_1_q[1]), .I0(register_1_q[0]), .char1(In[1]), .char0(In[0]),
    .O2(staterefresh_1_o0[2]), .O1(staterefresh_1_o0[1]), .O0(staterefresh_1_o0[0]));
  // Probe on staterefresh_1_o0
  Multiplexer #(.width(3)) multiplexer_1 (
    .in0(staterefresh_1_o0), .in1(3'b000), .out(multiplexer_1_out), .sel(reset));  // open: en
  Register #(.width(3)) register_1 (.D(multiplexer_1_out), .Q(register_1_q), .clk(clock_1_out));  // open: en, clr
  Clock clock_1 (.out(clock_1_out));
  // Probe on register_1_q
  stateOut stateout_1 (
    .I2(register_1_q[2]), .I1(register_1_q[1]), .I0(register_1_q[0]), .char1(In[1]), .char0(In[0]),
    .out(out_3));
endmodule

module stateOut (
  input  I2,
  input  I1,
  input  I0,
  input  char1,
  input  char0,
  output out
);

  wire not_1_out;

  not not_1 (not_1_out, char0);
  and and_1 (out, I1, I0, not_1_out);
endmodule
