// Logisim project P0_L0_GRF.circ as structural Verilog: 1 circuit, main circuit grf
module grf (
  input  clk,
  input  reset,
  input  WE,
  input  [4:0] A1,
  input  [4:0] A2,
  input  [4:0] A3,
  input  [31:0] WD,
  output [31:0] RD1,
  output [31:0] RD2
);

  wire [31:0] _1, _2, _3, _4, _5, _6, _7, _8, _9, _10, _11, _12, _13, _14, _15, _16, _17, _18, _19, _20, _21,
       _22, _23, _24, _25, _26, _27, _28, _29, _30, _31, _32, demultiplexer_1_out0, x1, x2, x3, x4, x5, x6,
       x7, x8, x9, x10, x11, x12, x13, x14, x15, x16, x17, x18, x19, x20, x21, x22, x23, x24, x25, x26, x27,
       x28, x29, x30, x31, x32;

  Register #(.width(32)) register_1 (.D(x1), .Q(_1), .clk(clk), .clr(reset));  // open: en
  Register #(.width(32)) register_2 (.D(x5), .Q(_5), .clk(clk), .clr(reset));  // open: en
  Register #(.width(32)) register_3 (.D(x9), .Q(_9), .clk(clk), .clr(reset));  // open: en
  Register #(.width(32)) register_4 (.D(x13), .Q(_13), .clk(clk), .clr(reset));  // open: en
  Register #(.width(32)) register_5 (.D(x17), .Q(_17), .clk(clk), .clr(reset));  // open: en
  Register #(.width(32)) register_6 (.D(x21), .Q(_21), .clk(clk), .clr(reset));  // open: en
  Register #(.width(32)) register_7 (.D(x25), .Q(_25), .clk(clk), .clr(reset));  // open: en
  Register #(.width(32)) register_8 (.D(x29), .Q(_29), .clk(clk), .clr(reset));  // open: en
  Register #(.width(32)) register_9 (.D(x2), .Q(_2), .clk(clk), .clr(reset));  // open: en
  Register #(.width(32)) register_10 (.D(x6), .Q(_6), .clk(clk), .clr(reset));  // open: en
  Register #(.width(32)) register_11 (.D(x10), .Q(_10), .clk(clk), .clr(reset));  // open: en
  Register #(.width(32)) register_12 (.D(x14), .Q(_14), .clk(clk), .clr(reset));  // open: en
  Register #(.width(32)) register_13 (.D(x18), .Q(_18), .clk(clk), .clr(reset));  // open: en
  Register #(.width(32)) register_14 (.D(x22), .Q(_22), .clk(clk), .clr(reset));  // open: en
  Register #(.width(32)) register_15 (.D(x26), .Q(_26), .clk(clk), .clr(reset));  // open: en
  Register #(.width(32)) register_16 (.D(x30), .Q(_30), .clk(clk), .clr(reset));  // open: en
  Register #(.width(32)) register_17 (.D(x3), .Q(_3), .clk(clk), .clr(reset));  // open: en
  Register #(.width(32)) register_18 (.D(x7), .Q(_7), .clk(clk), .clr(reset));  // open: en
  Register #(.width(32)) register_19 (.D(x11), .Q(_11), .clk(clk), .clr(reset));  // open: en
  Register #(.width(32)) register_20 (.D(x15), .Q(_15), .clk(clk), .clr(reset));  // open: en
  Register #(.width(32)) register_21 (.D(x19), .Q(_19), .clk(clk), .clr(reset));  // open: en
  Register #(.width(32)) register_22 (.D(x23), .Q(_23), .clk(clk), .clr(reset));  // open: en
  Register #(.width(32)) register_23 (.D(x27), .Q(_27), .clk(clk), .clr(reset));  // open: en
  Register #(.width(32)) register_24 (.D(x31), .Q(_31), .clk(clk), .clr(reset));  // open: en
  Register #(.width(32)) register_25 (.D(x4), .Q(_4), .clk(clk), .clr(reset));  // open: en
  Register #(.width(32)) register_26 (.D(x8), .Q(_8), .clk(clk), .clr(reset));  // open: en
  Register #(.width(32)) register_27 (.D(x12), .Q(_12), .clk(clk), .clr(reset));  // open: en
  Register #(.width(32)) register_28 (.D(x16), .Q(_16), .clk(clk), .clr(reset));  // open: en
  Register #(.width(32)) register_29 (.D(x20), .Q(_20), .clk(clk), .clr(reset));  // open: en
  Register #(.width(32)) register_30 (.D(x24), .Q(_24), .clk(clk), .clr(reset));  // open: en
  Register #(.width(32)) register_31 (.D(x28), .Q(_28), .clk(clk), .clr(reset));  // open: en
  Register #(.width(32)) register_32 (.D(x32), .Q(_32), .clk(clk), .clr(reset));  // open: en
  Demultiplexer #(.select(5), .width(32), .tristate("true")) demultiplexer_1 (
    .out0(demultiplexer_1_out0), .out1(x2), .out2(x3), .out3(x4), .out4(x5), .out5(x6), .out6(x7), .out7(x8),
    .out8(x9), .out9(x10), .out10(x11), .out11(x12), .out12(x13), .out13(x14), .out14(x15), .out15(x16),
    .out16(x17), .out17(x18), .out18(x19), .out19(x20), .out20(x21), .out21(x22), .out22(x23), .out23(x24),
    .out24(x25), .out25(x26), .out26(x27), .out27(x28), .out28(x29), .out29(x30), .out30(x31), .out31(x32),
    .in(WD), .sel(A3), .en(WE));
  assign x1 = {32{1'b0}} & demultiplexer_1_out0;  // AND_Gate and_1, 32 bits wide
  Multiplexer #(.select(5), .width(32)) multiplexer_1 (
    .in0(_1), .in1(_2), .in2(_3), .in3(_4), .in4(_5), .in5(_6), .in6(_7), .in7(_8), .in8(_9), .in9(_10),
    .in10(_11), .in11(_12), .in12(_13), .in13(_14), .in14(_15), .in15(_16), .in16(_17), .in17(_18),
    .in18(_19), .in19(_20), .in20(_21), .in21(_22), .in22(_23), .in23(_24), .in24(_25), .in25(_26),
    .in26(_27), .in27(_28), .in28(_29), .in29(_30), .in30(_31), .in31(_32), .out(RD1), .sel(A1));  // open: en
  Multiplexer #(.select(5), .width(32)) multiplexer_2 (
    .in0(_1), .in1(_2), .in2(_3), .in3(_4), .in4(_5), .in5(_6), .in6(_7), .in7(_8), .in8(_9), .in9(_10),
    .in10(_11), .in11(_12), .in12(_13), .in13(_14), .in14(_15), .in15(_16), .in16(_17), .in17(_18),
    .in18(_19), .in19(_20), .in20(_21), .in21(_22), .in22(_23), .in23(_24), .in24(_25), .in25(_26),
    .in26(_27), .in27(_28), .in28(_29), .in29(_30), .in30(_31), .in31(_32), .out(RD2), .sel(A2));  // open: en
endmodule
