// Logisim project P0_L1_ftoi .circ as structural Verilog: 1 circuit, main circuit ftoi
module ftoi (
  input  [15:0] in_1,
  output [31:0] out_2
);

  wire comparator_1_eq, comparator_2_lt, or_1_out;
  wire [4:0] subtractor_1_out;
  wire [31:0] adder_1_out, bit_extender_1_out, multiplexer_2_out, not_1_out, or_2_out, shifter_1_out, x;

  Comparator #(.width(5), .mode("unsigned")) comparator_1 (
    .a(in_1[14:10]), .b({5{1'b1}}), .eq(comparator_1_eq));  // open: gt, lt
  Comparator #(.width(5), .mode("unsigned")) comparator_2 (
    .a(in_1[14:10]), .b(5'b01111), .lt(comparator_2_lt));  // open: gt, eq
  assign not_1_out = ~x;  // NOT_Gate not_1, 32 bits wide
  or or_1 (or_1_out, comparator_1_eq, comparator_2_lt);
  Adder #(.width(32)) adder_1 (.a(not_1_out), .b(32'h1), .out(adder_1_out));  // open: cin, cout
  Multiplexer #(.width(32)) multiplexer_1 (
    .in0(multiplexer_2_out), .in1({32{1'b0}}), .out(out_2), .sel(or_1_out));  // open: en
  Subtractor #(.width(5)) subtractor_1 (.a(in_1[14:10]), .b(5'b01111), .out(subtractor_1_out));  // open: bin, bout
  assign or_2_out = 32'h80000000 | adder_1_out;  // OR_Gate or_2, 32 bits wide
  assign bit_extender_1_out = {{21{1'b0}}, {1'b1, in_1[9:0]}};  // Bit_Extender bit_extender_1
  // Probe on subtractor_1_out
  // Probe on bit_extender_1_out
  Shifter #(.width(32)) shifter_1 (.in(bit_extender_1_out), .\dist (subtractor_1_out), .out(shifter_1_out));
  Multiplexer #(.width(32)) multiplexer_2 (
    .in0(x), .in1(or_2_out), .out(multiplexer_2_out), .sel(in_1[15]));  // open: en
  // Probe on shifter_1_out
  Shifter #(.width(32), .shift("lr")) shifter_2 (.in(shifter_1_out), .\dist (5'b01010), .out(x));
  // Probe on x

  // Other names for the same wires on the sheet: 小数位[9:0] = in_1[9:0]; 指数[4:0] = in_1[14:10]; sign = in_1[15]
endmodule
