// Logisim project P0_L1_navigation_2020.circ as structural Verilog: 2 circuits, main circuit navigation
module navigation (
  input  [1:0] dir,
  input  clk,
  input  reset,
  output arrive,
  output out_5
);

  wire comparator_1_eq;
  wire [2:0] register_1_q, staterefresh_1_o0;

  stateRefresh staterefresh_1 (
    .dir1(dir[1]), .dir0(dir[0]), .I2(register_1_q[2]), .I1(register_1_q[1]), .I0(register_1_q[0]),
    .O2(staterefresh_1_o0[2]), .O1(staterefresh_1_o0[1]), .O0(staterefresh_1_o0[0]));
  // Probe on staterefresh_1_o0
  Register #(.width(3)) register_1 (.D(staterefresh_1_o0), .Q(register_1_q), .clk(clk), .clr(reset));  // open: en
  Comparator #(.width(3), .mode("unsigned")) comparator_1 (
    .a(register_1_q), .b(staterefresh_1_o0), .eq(comparator_1_eq));  // open: gt, lt
  // Probe on register_1_q
  Register #(.width(1)) register_2 (.D(comparator_1_eq), .Q(out_5), .clk(clk), .clr(reset));  // open: en
  Comparator #(.width(3), .mode("unsigned")) comparator_2 (.a(3'b100), .b(register_1_q), .eq(arrive));  // open: gt, lt
endmodule

module stateRefresh (
  input  dir1,
  input  dir0,
  input  I2,
  input  I1,
  input  I0,
  output O2,
  output O1,
  output O0
);

  wire and_1_out, and_2_out, and_3_out, and_4_out, and_5_out, and_6_out, and_7_out, and_8_out, and_9_out,
       and_10_out, and_11_out, not_1_out, not_2_out, not_3_out, not_4_out, not_5_out, not_6_out, not_7_out,
       not_8_out, not_9_out, not_10_out, not_11_out, not_12_out, not_13_out, not_14_out, not_15_out,
       not_16_out, not_17_out, not_18_out, not_19_out, not_20_out, not_21_out, not_22_out, not_23_out,
       not_24_out, not_25_out, not_26_out, not_27_out;

  not not_1 (not_1_out, dir1);
  not not_2 (not_2_out, dir0);
  not not_3 (not_3_out, I2);
  not not_4 (not_4_out, I0);
  not not_5 (not_5_out, dir1);
  not not_6 (not_6_out, I2);
  not not_7 (not_7_out, dir1);
  not not_8 (not_8_out, dir0);
  not not_9 (not_9_out, I2);
  not not_10 (not_10_out, dir1);
  not not_11 (not_11_out, I2);
  not not_12 (not_12_out, I1);
  not not_13 (not_13_out, dir1);
  not not_14 (not_14_out, I2);
  not not_15 (not_15_out, I0);
  not not_16 (not_16_out, dir0);
  not not_17 (not_17_out, I2);
  not not_18 (not_18_out, I0);
  not not_19 (not_19_out, I2);
  not not_20 (not_20_out, dir1);
  not not_21 (not_21_out, dir0);
  not not_22 (not_22_out, I2);
  not not_23 (not_23_out, I1);
  not not_24 (not_24_out, dir0);
  not not_25 (not_25_out, I2);
  not not_26 (not_26_out, I2);
  not not_27 (not_27_out, I2);
  and and_1 (and_1_out, not_1_out, not_2_out, not_3_out, I1, not_4_out);
  and and_2 (and_2_out, not_5_out, dir0, not_6_out, I1, I0);
  and and_3 (and_3_out, not_7_out, not_8_out, not_9_out, I0);
  and and_4 (and_4_out, not_10_out, not_11_out, not_12_out, I0);
  and and_5 (and_5_out, not_13_out, dir0, not_14_out, I1, not_15_out);
  and and_6 (and_6_out, dir1, not_16_out, not_17_out, I1, not_18_out);
  and and_7 (and_7_out, dir1, dir0, not_19_out, I1, I0);
  and and_8 (and_8_out, not_20_out, not_21_out, not_22_out, not_23_out);
  and and_9 (and_9_out, not_24_out, not_25_out, I1, I0);
  and and_10 (and_10_out, dir1, dir0, not_26_out, I0);
  and and_11 (and_11_out, dir1, dir0, not_27_out, I1);
  or or_1 (O2, and_1_out, and_2_out);
  or or_2 (O1, and_3_out, and_4_out, and_5_out, and_6_out, and_7_out);
  or or_3 (O0, and_8_out, and_9_out, and_10_out, and_11_out);
endmodule
