// Logisim project 单周期cpu镜像.circ as structural Verilog: 8 circuits, main circuit main
module main (
  input  reset,
  output [31:0] out_2,
  output [31:0] out_3,
  output out_4,
  output [4:0] out_5,
  output [31:0] out_6,
  output out_7,
  output [31:0] out_8,
  output [31:0] out_9
);

  wire alu_1_zero, Bsel, clock_out, EXTop, WRsel;
  wire [1:0] NPCop, WDsel;
  wire [3:0] ALUop;
  wire [31:0] dm_1_rd, ext_1__32bit, multiplexer_3_out, npc_1_npc, npc_1_pc___4, PC, rf_1_rd1;

  Clock clock (.out(clock_out));
  NPC npc_1 (
    .Imm16(out_2[15:0]), .Imm26(out_2[25:0]), .Zero(alu_1_zero), .RA32(rf_1_rd1), .PC___4(npc_1_pc___4),
    .NPC(npc_1_npc), .PC(PC), .NPCop(NPCop));
  Register #(.width(32)) u_PC (.D(npc_1_npc), .Q(PC), .clk(clock_out), .clr(reset));  // open: en
  IM im_1 (.PC(PC), .Instruction(out_2));
  Control control_1 (
    .NPCop(NPCop), .WRsel(WRsel), .EXTop(EXTop), .WDsel(WDsel), .RFWr(out_4), .Bsel(Bsel), .ALUop(ALUop),
    .DMWr(out_7), .opcode(out_2[31:26]), .funct(out_2[5:0]));
  Multiplexer #(.width(5)) multiplexer_1 (
    .in0(out_2[20:16]), .in1(out_2[15:11]), .out(out_5), .sel(WRsel));  // open: en
  EXT ext_1 (.Imm16(out_2[15:0]), ._32bit(ext_1__32bit), .EXTop(EXTop));
  Adder #(.width(32)) adder_1 (.a(PC), .b(32'h3000), .out(out_3));  // open: cin, cout
  Multiplexer #(.select(2), .width(32)) multiplexer_2 (
    .in0(out_8), .in1(dm_1_rd), .in2(npc_1_pc___4), .out(out_6), .sel(WDsel));  // open: in3, en
  RF rf_1 (
    .A1(out_2[25:21]), .A2(out_2[20:16]), .A3(out_5), .WD(out_6), .RD1(rf_1_rd1), .RD2(out_9),
    .clk(clock_out), .reset(reset), .RFWr(out_4));
  Multiplexer #(.width(32)) multiplexer_3 (
    .in0(out_9), .in1(ext_1__32bit), .out(multiplexer_3_out), .sel(Bsel));  // open: en
  ALU alu_1 (
    .Zero(alu_1_zero), .C(out_8), .A(rf_1_rd1), .B(multiplexer_3_out), .ALUop(ALUop));  // open: Less_or_Equal, Less
  DM dm_1 (.A(out_8), .WD(out_9), .DMWr(out_7), .RD(dm_1_rd), .Reset(reset), .Clk(clock_out));

  // Other names for the same wires on the sheet: DMWr = out_7; Instr[31:0] = out_2; MemAddr[31:0] = out_8;
  //   MemData[31:0] = out_9; RegAddr[4:0] = out_5; RegData[31:0] = out_6; RFWr = out_4

  // Notes on the sheet:
  //   jr指令
  //   opcode
  //   funct
  //   rs
  //   rt
  //   rd
  //   shamt
  //   Imm16
  //   Imm26
endmodule

module NPC (
  input  [31:0] PC,
  input  [15:0] Imm16,
  input  Zero,
  input  [1:0] NPCop,
  input  [25:0] Imm26,
  input  [31:0] RA32,
  output [31:0] PC___4,
  output [31:0] NPC
);

  wire [31:0] adder_2_out, adder_3_out, bit_extender_1_out, bit_extender_2_out, multiplexer_1_out;

  Adder #(.width(32)) adder_1 (.a(PC), .b(32'h4), .out(PC___4));  // open: cin, cout
  assign bit_extender_1_out = {{14{Imm16[15]}}, {Imm16, 2'b00}};  // Bit_Extender bit_extender_1
  assign bit_extender_2_out = {{4{Imm26[25]}}, {Imm26, 2'b00}};  // Bit_Extender bit_extender_2
  Adder #(.width(32)) adder_2 (.a(PC___4), .b(bit_extender_1_out), .out(adder_2_out));  // open: cin, cout
  Adder #(.width(32)) adder_3 (.a(PC___4), .b(bit_extender_2_out), .out(adder_3_out));  // open: cin, cout
  Multiplexer #(.width(32)) multiplexer_1 (
    .in0(PC___4), .in1(adder_2_out), .out(multiplexer_1_out), .sel(Zero));  // open: en
  Multiplexer #(.select(2), .width(32)) multiplexer_2 (
    .in0(PC___4), .in1(multiplexer_1_out), .in2(adder_3_out), .in3(RA32), .out(NPC), .sel(NPCop), .en(1'b1));
endmodule

module IM (
  input  [31:0] PC,
  output [31:0] Instruction
);

  ROM #(.addrWidth(12), .dataWidth(32)) rom_1 (.addr(PC[13:2]), .data(Instruction));  // open: sel

  // Notes on the sheet:
  //   contents of rom_1 (hex, n*v repeats v):
  //   34011cf4 34020002 34039dc4 34040001 34055117 3406c97d 3407be7e 3408e3c3 34091264 340aba60 340b0002
  //   340cd8e3 340d5437 340e78e5 340f0001 34100001 3411b829 34125d1a 3413e42a 3414ba7f 3415b523 3416fffe
  //   3417fffe 3418ec3d 34197ff3 341afffe 341bb535 341ce8cc 341dec09 341effff 341fe9c1 11d40008 273f020
  //   26dd022 36ff2697 340001b0 ac15030c 340304b8 8c63045c 3c0e3668 22f4020 7b6822 34620001 340101d4
  //   ac2f0150 34010054 8c2400a4 3c170001 37007ee3 3402fffd 2bf9022 3829820 340901cc ad390790 c1a022
  //   11190008 28d020 2021822 3548fffe 340201dc ac4e03f0 340400a4 8c9c0400 3c0eb83b 3718020 1220022
  //   3758fffd 340f0198 ade501a0 340b01ac 8d6103b4 3c0dffff 13b30008 361d820 34b1822 37c6fffd 34170584
  //   aee704a0 34130af4 8e77004c 3c1a0002 3c6020 35f1822 35bd25c7 341205f4 ae400060 340407d8 8c930380
  //   3c0c0002 0 11160009 340d03e8 340603e8 3c20822 365ffffe 341703dc aee9044c 341a0358 8f5e07dc 3c120001
  //   21bf820 c42822 35764b02 34040098 ac9a0160 341201d8 8e48063c 3c15fffd 34090304 ad2708a4 0 1f0a822
  //   37aa7809 0 3c09ffff 179c020 239f020 341e0460 afda05c0 3c057333 34180004 8f190a28 3c1deebf 34260001 0
  //   341800cc 8f0608ec 341f0044 afec09c8 3d0d820 35bd2549 3c002181 12bd0009 3305820 340303e8 340a03e8
  //   371f96f2 34000474 ac090484 34000044 8c1d05dc 3c1868a9 3e89820 264f022 3690ffff 3419035c af330848
  //   340d04c4 8da50640 3c092da3 340e01d8 adc20750 34070610 ace301c8 3c0d0000 3c1dfffe 125d0008 146a020
  //   3cc7822 35770001 34110288 ae2e08cc 3419023c 8f380578 3c14954d 2f32020 3cbc822 36d00000 34140104
  //   ae8b0610 34060154 8cc1059c 3c16ffff 0 1f8a020 34090284 ad3e05c0 34060344 8cdf0244 3c100002 341503f0
  //   aea50300 3415052c 8ea205f4 1644820 0 12280008 1c3c820 3dfc822 34b4fdcd 341d0694 afb902b4 341c01b8
  //   8f9800bc 3c1c41a4 1643820 27dc822 36000002 340b0258 ad6e0064 34050530 8cbb0560 3c1dfffe 341e08f0
  //   8fc40238 634020 34150084 8ea00ae8 34170000 8ee807dc 35e70001 3156820 0 35266bae 3598fffe 351b0002
  //   3d13022 341106b8 ae3f03a8 3426676e 34190028 8f2c0944 3601f346 1347020 c86020 37a56af0 36342293 0 0
  //   267e820 340d02a8 ada106b0 340c0104 ad9906e0 37bcc406 120c0008 1572020 1c8f022 35b3992d 34000328
  //   ac060074 34030444 8c740518 3c10af88 9ae020 32f022 35a8fffd 3404012c ac980a20 34110028 8e3c0a50
  //   3c1f0001 35d3ffff 3c197828 3410007c 8e030aa4 3779fffe 0 0 13120008 780020 32ed822 34d10002 34040038
  //   ac9f0b44 34110078 8e2e0064 3c1effff 1b44820 697822 34d22c56 341b0010 af680b50 341302a4 8e62082c
  //   3c11fffd 3c1531d4 3c06b23b 3c1190e7 3441ffff 64b020 0 0 0 340a0014 8d4b09d0 172b020 1ee1020 0 e4b822
  //   340c0018 8d8e01a4 0 1c38822 0 0 3769ffff 3c035d8b 137c0009 13a5820 341c03e8 341e03e8 359d0002
  //   34160010 aece0a1c 34010268 8c3906d0 3c01f45d 22f8020 3b7e822 35fd51ad 34120358 ae5d05c8 340f00c4
  //   8de70a70 3c07fffe 10b80008 149b020 17a7022 37fc5864 34100490 ae1a0500 34130084 8e790a58 3c14cd39
  //   1bd1020 340703e8 340003e8 3697cfe1 3414086c ae8b0148 34190078 8f3e09e8 3c1c0970 3c010001 2b90020
  //   101e0009 33f9820 341103e8 340503e8 36ed0002 340f0298 adeb08a0 340d01dc 8dae0960 3c0f0002 1406820
  //   341e03e8 341703e8 358b5d49 3400035c ac1f0220 34000028 8c0d09f0 3c1d64d4 37310b23 f3b820 3d8b820
  //   3ab2022 349dfffe 2419022 341a02f8 8f440200 340c0564 ad9d00a0 10690008 1893020 347022 36270000
  //   341606c4 aec80218 34130014 8e6c08d8 3c010001 682020 356f822 365effff 34070170 ace9001c 34160010
  //   8ec90b64 3c134215 1d57022 36d5822 0 37fa820 3c0b3c34 3094020 0 34070838 8cf10160 348ca09a 35efcfea
  //   10d40008 2cf8020 36ea822 35020001 341901a8 af2a0268 341b000c 8f730768 3c07ffff 4c3020 cd822 36985949
  //   3411048c ae31041c 34130480 8e6e04f0 3c1afffe 340b00d4 ad790a70 341b0148 af7d0930 341003e8 341a03e8
  //   10be0008 1bb7020 1984022 348afffe 3405056c aca905f8 340e0028 8dcb08d8 3c1bc874 1ca9820 1ccc822
  //   360e8608 3401013c ac2a0a54 340307d8 8c7900e4 3c0c95cb 2abe820 106d0008 2801820 1cbd022 37d8ffff
  //   34040058 ac920a80 341a0880 8f43010c 3c090002 341e03e8 341b03e8 c0a822 35a4fffd 340904b8 ad210074
  //   34070a48 8cf00048 3c018cf6 17ac022 1aa7820 0 340603e8 340f03e8 340d0078 8da30ab0 35406670 34150014
  //   8eb20b0c 340f05c0 8de801b0 116d0008 253b820 2651022 351eb580 341b01b0 af720984 340b0134 8d660a54
  //   3c0e43b7 3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
endmodule

module EXT (
  input  EXTop,
  input  [15:0] Imm16,
  output [31:0] _32bit
);

  wire [31:0] bit_extender_1_out, bit_extender_2_out;

  assign bit_extender_1_out = {{16{1'b0}}, Imm16};  // Bit_Extender bit_extender_1
  assign bit_extender_2_out = {{16{Imm16[15]}}, Imm16};  // Bit_Extender bit_extender_2
  Multiplexer #(.width(32)) multiplexer_1 (
    .in0(bit_extender_1_out), .in1(bit_extender_2_out), .out(_32bit), .sel(EXTop));  // open: en
endmodule

module RF (
  input  clk,
  input  reset,
  input  RFWr,
  input  [4:0] A1,
  input  [4:0] A2,
  input  [4:0] A3,
  input  [31:0] WD,
  output [31:0] RD1,
  output [31:0] RD2
);

  wire [31:0] _1, _2, _3, _4, _5, _6, _7, _8, _9, _10, _11, _12, _13, _14, _15, _16, _17, _18, _19, _20, _21,
       _22, _23, _24, _25, _26, _27, _28, _29, _30, _31, _32, demultiplexer_1_out0, x1, x2, x3, x4, x5, x6,
       x7, x8, x9, x10, x11, x12, x13, x14, x15, x16, x17, x18, x19, x20, x21, x22, x23, x24, x25, x26, x27,
       x28, x29, x30, x31, x32;

  Register #(.width(32)) register_1 (.D(x1), .Q(_1), .clk(clk), .clr(reset));  // open: en
  Register #(.width(32)) register_2 (.D(x5), .Q(_5), .clk(clk), .clr(reset));  // open: en
  Register #(.width(32)) register_3 (.D(x9), .Q(_9), .clk(clk), .clr(reset));  // open: en
  Register #(.width(32)) register_4 (.D(x13), .Q(_13), .clk(clk), .clr(reset));  // open: en
  Register #(.width(32)) register_5 (.D(x17), .Q(_17), .clk(clk), .clr(reset));  // open: en
  Register #(.width(32)) register_6 (.D(x21), .Q(_21), .clk(clk), .clr(reset));  // open: en
  Register #(.width(32)) register_7 (.D(x25), .Q(_25), .clk(clk), .clr(reset));  // open: en
  Register #(.width(32)) register_8 (.D(x29), .Q(_29), .clk(clk), .clr(reset));  // open: en
  Register #(.width(32)) register_9 (.D(x2), .Q(_2), .clk(clk), .clr(reset));  // open: en
  Register #(.width(32)) register_10 (.D(x6), .Q(_6), .clk(clk), .clr(reset));  // open: en
  Register #(.width(32)) register_11 (.D(x10), .Q(_10), .clk(clk), .clr(reset));  // open: en
  Register #(.width(32)) register_12 (.D(x14), .Q(_14), .clk(clk), .clr(reset));  // open: en
  Register #(.width(32)) register_13 (.D(x18), .Q(_18), .clk(clk), .clr(reset));  // open: en
  Register #(.width(32)) register_14 (.D(x22), .Q(_22), .clk(clk), .clr(reset));  // open: en
  Register #(.width(32)) register_15 (.D(x26), .Q(_26), .clk(clk), .clr(reset));  // open: en
  Register #(.width(32)) register_16 (.D(x30), .Q(_30), .clk(clk), .clr(reset));  // open: en
  Register #(.width(32)) register_17 (.D(x3), .Q(_3), .clk(clk), .clr(reset));  // open: en
  Register #(.width(32)) register_18 (.D(x7), .Q(_7), .clk(clk), .clr(reset));  // open: en
  Register #(.width(32)) register_19 (.D(x11), .Q(_11), .clk(clk), .clr(reset));  // open: en
  Register #(.width(32)) register_20 (.D(x15), .Q(_15), .clk(clk), .clr(reset));  // open: en
  Register #(.width(32)) register_21 (.D(x19), .Q(_19), .clk(clk), .clr(reset));  // open: en
  Register #(.width(32)) register_22 (.D(x23), .Q(_23), .clk(clk), .clr(reset));  // open: en
  Register #(.width(32)) register_23 (.D(x27), .Q(_27), .clk(clk), .clr(reset));  // open: en
  Register #(.width(32)) register_24 (.D(x31), .Q(_31), .clk(clk), .clr(reset));  // open: en
  Register #(.width(32)) register_25 (.D(x4), .Q(_4), .clk(clk), .clr(reset));  // open: en
  Register #(.width(32)) register_26 (.D(x8), .Q(_8), .clk(clk), .clr(reset));  // open: en
  Register #(.width(32)) register_27 (.D(x12), .Q(_12), .clk(clk), .clr(reset));  // open: en
  Register #(.width(32)) register_28 (.D(x16), .Q(_16), .clk(clk), .clr(reset));  // open: en
  Register #(.width(32)) register_29 (.D(x20), .Q(_20), .clk(clk), .clr(reset));  // open: en
  Register #(.width(32)) register_30 (.D(x24), .Q(_24), .clk(clk), .clr(reset));  // open: en
  Register #(.width(32)) register_31 (.D(x28), .Q(_28), .clk(clk), .clr(reset));  // open: en
  Register #(.width(32)) register_32 (.D(x32), .Q(_32), .clk(clk), .clr(reset));  // open: en
  Demultiplexer #(.select(5), .width(32), .tristate("true")) demultiplexer_1 (
    .out0(demultiplexer_1_out0), .out1(x2), .out2(x3), .out3(x4), .out4(x5), .out5(x6), .out6(x7), .out7(x8),
    .out8(x9), .out9(x10), .out10(x11), .out11(x12), .out12(x13), .out13(x14), .out14(x15), .out15(x16),
    .out16(x17), .out17(x18), .out18(x19), .out19(x20), .out20(x21), .out21(x22), .out22(x23), .out23(x24),
    .out24(x25), .out25(x26), .out26(x27), .out27(x28), .out28(x29), .out29(x30), .out30(x31), .out31(x32),
    .in(WD), .sel(A3), .en(RFWr));
  assign x1 = {32{1'b0}} & demultiplexer_1_out0;  // AND_Gate and_1, 32 bits wide
  Multiplexer #(.select(5), .width(32)) multiplexer_1 (
    .in0(_1), .in1(_2), .in2(_3), .in3(_4), .in4(_5), .in5(_6), .in6(_7), .in7(_8), .in8(_9), .in9(_10),
    .in10(_11), .in11(_12), .in12(_13), .in13(_14), .in14(_15), .in15(_16), .in16(_17), .in17(_18),
    .in18(_19), .in19(_20), .in20(_21), .in21(_22), .in22(_23), .in23(_24), .in24(_25), .in25(_26),
    .in26(_27), .in27(_28), .in28(_29), .in29(_30), .in30(_31), .in31(_32), .out(RD1), .sel(A1));  // open: en
  Multiplexer #(.select(5), .width(32)) multiplexer_2 (
    .in0(_1), .in1(_2), .in2(_3), .in3(_4), .in4(_5), .in5(_6), .in6(_7), .in7(_8), .in8(_9), .in9(_10),
    .in10(_11), .in11(_12), .in12(_13), .in13(_14), .in14(_15), .in15(_16), .in16(_17), .in17(_18),
    .in18(_19), .in19(_20), .in20(_21), .in21(_22), .in22(_23), .in23(_24), .in24(_25), .in25(_26),
    .in26(_27), .in27(_28), .in28(_29), .in29(_30), .in30(_31), .in31(_32), .out(RD2), .sel(A2));  // open: en

  // Other names for the same wires on the sheet: WE = RFWr
endmodule

module ALU (
  input  [31:0] A,
  input  [31:0] B,
  input  [3:0] ALUop,
  output Less_or_Equal,
  output Zero,
  output Less,
  output [31:0] C
);

  wire comparator_1_gt;
  wire [31:0] adder_1_out, and_1_out, or_1_out, shifter_1_out, shifter_2_out, shifter_3_out, subtractor_1_out;

  Adder #(.width(32)) adder_1 (.a(B), .b(A), .out(adder_1_out));  // open: cin, cout
  Subtractor #(.width(32)) subtractor_1 (.a(A), .b(B), .out(subtractor_1_out));  // open: bin, bout
  assign or_1_out = B | A;  // OR_Gate or_1, 32 bits wide
  assign and_1_out = B & A;  // AND_Gate and_1, 32 bits wide
  Shifter #(.width(32)) shifter_1 (.in(A), .\dist (B[4:0]), .out(shifter_1_out));
  Shifter #(.width(32), .shift("ar")) shifter_2 (.in(A), .\dist (B[4:0]), .out(shifter_2_out));
  Shifter #(.width(32), .shift("lr")) shifter_3 (.in(A), .\dist (B[4:0]), .out(shifter_3_out));
  Comparator #(.width(32)) comparator_1 (.a(B), .b(A), .gt(comparator_1_gt), .eq(Zero), .lt(Less));
  not not_1 (Less_or_Equal, comparator_1_gt);
  Multiplexer #(.select(4), .width(32)) multiplexer_1 (
    .in0(adder_1_out), .in1(subtractor_1_out), .in2(or_1_out), .in3(and_1_out), .in4({B[15:0], {16{1'b0}}}),
    .in5(shifter_1_out), .in6(shifter_2_out), .in7(shifter_3_out), .out(C), .sel(ALUop));  // open: in8, in9, in10, in11, in12, in13, in14, in15, en

  // Notes on the sheet:
  //   lui 加载立即数到高16位
  //   逻辑左、算数左
  //   算数右
  //   逻辑右
endmodule

module DM (
  input  [31:0] A,
  input  [31:0] WD,
  input  DMWr,
  input  Reset,
  input  Clk,
  output [31:0] RD
);

  RAM #(.addrWidth(12), .dataWidth(32), .bus("separate")) ram_1 (
    .addr(A[11:0]), .din(WD), .data(RD), .str(DMWr), .clk(Clk), .clr(Reset));  // open: sel, ld
endmodule

module Control (
  input  [5:0] opcode,
  input  [5:0] funct,
  output [1:0] NPCop,
  output WRsel,
  output EXTop,
  output [1:0] WDsel,
  output RFWr,
  output Bsel,
  output [3:0] ALUop,
  output DMWr
);

  wire and_1_out, and_2_out, comparator_1_eq, comparator_2_eq, comparator_3_eq, comparator_4_eq,
       comparator_5_eq, comparator_6_eq, comparator_7_eq, comparator_8_eq, comparator_9_eq;

  Comparator #(.width(6), .mode("unsigned")) comparator_1 (
    .a(opcode), .b({6{1'b0}}), .eq(comparator_1_eq));  // open: gt, lt
  Comparator #(.width(6), .mode("unsigned")) comparator_2 (
    .a(opcode), .b(6'b001101), .eq(comparator_2_eq));  // open: gt, lt
  Comparator #(.width(6), .mode("unsigned")) comparator_3 (
    .a(opcode), .b(6'b100011), .eq(comparator_3_eq));  // open: gt, lt
  Comparator #(.width(6), .mode("unsigned")) comparator_4 (
    .a(opcode), .b(6'b101011), .eq(comparator_4_eq));  // open: gt, lt
  Comparator #(.width(6), .mode("unsigned")) comparator_5 (
    .a(opcode), .b(6'b000100), .eq(comparator_5_eq));  // open: gt, lt
  Comparator #(.width(6), .mode("unsigned")) comparator_6 (
    .a(opcode), .b(6'b001111), .eq(comparator_6_eq));  // open: gt, lt
  Comparator #(.width(6), .mode("unsigned")) comparator_7 (
    .a(opcode), .b({6{1'b0}}), .eq(comparator_7_eq));  // open: gt, lt
  Comparator #(.width(6), .mode("unsigned")) comparator_8 (
    .a(funct), .b(6'b100000), .eq(comparator_8_eq));  // open: gt, lt
  Comparator #(.width(6), .mode("unsigned")) comparator_9 (
    .a(funct), .b(6'b100010), .eq(comparator_9_eq));  // open: gt, lt
  and and_1 (and_1_out, comparator_1_eq, comparator_8_eq);
  and and_2 (and_2_out, comparator_1_eq, comparator_9_eq);
  or or_1 (NPCop[0], 1'b0, comparator_5_eq);
  buf or_2 (NPCop[1], 1'b0);  // OR_Gate
  or or_3 (WRsel, and_1_out, and_2_out, 1'b0);
  or or_4 (EXTop, 1'b0, comparator_3_eq, comparator_4_eq, comparator_5_eq);
  or or_5 (WDsel[0], 1'b0, comparator_3_eq);
  buf or_6 (WDsel[1], 1'b0);  // OR_Gate
  or or_7 (RFWr, 1'b0, and_1_out, and_2_out, comparator_2_eq, comparator_3_eq, comparator_6_eq);
  or or_8 (Bsel, 1'b0, comparator_2_eq, comparator_3_eq, comparator_4_eq, comparator_6_eq);
  or or_9 (ALUop[0], 1'b0, and_2_out, comparator_5_eq);
  or or_10 (ALUop[1], 1'b0, comparator_2_eq);
  or or_11 (ALUop[2], 1'b0, comparator_6_eq);
  buf or_12 (ALUop[3], 1'b0);  // OR_Gate
  or or_13 (DMWr, 1'b0, comparator_4_eq);

  // Notes on the sheet:
  //   add
  //   sub
  //   ori
  //   lw
  //   sw
  //   beq
  //   lui
  //   nop
endmodule
