// Logisim project 流水线.circ as structural Verilog: 14 circuits, main circuit main
module main (
);

  wire ADD8_out_2, d_cmpSuc, D_EXT_out_3, d_extOp, D_NPC_out_8, d_npcOp, d_regAddr, d_regAddrSel, D_RF_out_8,
       d_rs, DE_out_8, DE_out_9, DE_out_10, DE_out_11, DE_out_12, DE_out_13, DE_out_14, E_ALU_out_4, e_aluOp,
       e_Bsel, EM_out_7, EM_out_8, EM_out_9, EM_out_10, EM_out_11, EM_out_13, F_IM_out_2, F_PC_out_3,
       FD_out_4, FD_out_5, M_DM_out_5, m_dmWr, multiplexer_2_out, MW_out_7, MW_out_8, MW_out_9, w_pc,
       w_regAddr, w_regData, w_regDataSel, w_regWr;

  PC F_PC (.in_2(D_NPC_out_8), .out_3(F_PC_out_3));  // open: in_1
  IM F_IM (.in_1(F_PC_out_3), .out_2(F_IM_out_2));
  FD FD (.in_2(F_PC_out_3), .in_3(F_IM_out_2), .out_4(FD_out_4), .out_5(FD_out_5));  // open: in_1
  Control D_Control (
    .in_1(FD_out_5), .out_2(d_npcOp), .out_3(d_regAddrSel), .out_4(d_extOp));  // open: out_5, out_6, out_7, out_8, out_9
  Multiplexer #(.select(2)) multiplexer_1 (
    .in0(FD_out_5), .in1(FD_out_5), .in2(1'b1), .out(d_regAddr), .en(d_regAddrSel));  // open: in3, sel
  RF D_RF (
    .in_1(w_pc), .in_2(w_regWr), .in_3(FD_out_5), .in_4(FD_out_5), .in_5(w_regAddr), .in_6(w_regData),
    .out_7(d_rs), .out_8(D_RF_out_8));
  EXT D_EXT (.in_1(d_extOp), .in_2(FD_out_5), .out_3(D_EXT_out_3));
  NPC D_NPC (
    .in_1(d_cmpSuc), .in_2(FD_out_4), .in_3(d_npcOp), .in_4(F_PC_out_3), .in_5(FD_out_5), .in_6(FD_out_5),
    .in_7(d_rs), .out_8(D_NPC_out_8));
  Comparator #(.width(1), .mode("unsigned")) comparator_1 (.a(d_rs), .b(D_RF_out_8), .eq(d_cmpSuc));  // open: gt, lt
  DE DE (
    .in_1(FD_out_4), .in_2(FD_out_5), .in_4(d_rs), .in_5(D_RF_out_8), .in_6(D_EXT_out_3), .in_7(d_regAddr),
    .out_8(DE_out_8), .out_9(DE_out_9), .out_10(DE_out_10), .out_11(DE_out_11), .out_12(DE_out_12),
    .out_13(DE_out_13), .out_14(DE_out_14));  // open: in_3
  Control E_Control (
    .in_1(DE_out_9), .out_7(e_Bsel), .out_8(e_aluOp));  // open: out_2, out_3, out_4, out_5, out_6, out_9
  Multiplexer multiplexer_2 (.in0(DE_out_11), .in1(DE_out_12), .out(multiplexer_2_out), .en(e_Bsel));  // open: sel
  ALU E_ALU (.in_2(DE_out_10), .in_3(multiplexer_2_out), .out_4(E_ALU_out_4), .in_1(e_aluOp));
  EM EM (
    .in_1(DE_out_8), .in_2(DE_out_9), .in_3(E_ALU_out_4), .in_4(DE_out_13), .in_5(DE_out_11),
    .out_7(EM_out_7), .out_8(EM_out_8), .out_9(EM_out_9), .out_10(EM_out_10), .out_11(EM_out_11),
    .out_13(EM_out_13));  // open: in_6, out_12
  Control M_Control (.in_1(EM_out_8), .out_9(m_dmWr));  // open: out_2, out_3, out_4, out_5, out_6, out_7, out_8
  DM M_DM (.in_2(m_dmWr), .in_3(EM_out_9), .in_4(EM_out_11), .out_5(M_DM_out_5), .in_1(EM_out_7));
  MW MW (
    .in_1(EM_out_7), .in_2(EM_out_8), .in_3(M_DM_out_5), .in_4(EM_out_9), .in_5(EM_out_10), .out_6(w_pc),
    .out_7(MW_out_7), .out_8(MW_out_8), .out_9(MW_out_9), .out_10(w_regAddr));
  ADD8 ADD8 (.in_1(w_pc), .out_2(ADD8_out_2));
  Control W_Control (
    .in_1(MW_out_7), .out_5(w_regWr), .out_6(w_regDataSel));  // open: out_2, out_3, out_4, out_7, out_8, out_9
  Multiplexer #(.select(2)) multiplexer_3 (
    .in0(ADD8_out_2), .in1(MW_out_8), .in2(MW_out_9), .out(w_regData), .en(w_regDataSel));  // open: in3, sel

  // Notes on the sheet:
  //   f_pc
  //   f_instr
  //   d_pc
  //   d_instr
  //   [15:11]
  //   [25:21]
  //   [20:16]
  //   [15:0]
  //   [25:0]
  //   d_rs
  //   d_rt
  //   d_imm32
  //   e_pc
  //   e_instr
  //   e_rs
  //   e_rt
  //   e_imm32
  //   e_regAddr
  //   e_tnew
  //   e_aluC
  //   m_pc
  //   m_instr
  //   m_aluC
  //   m_regAddr
  //   m_rt
  //   m_tnew
  //   m_dmData
  //   w_pc
  //   w_instr
  //   w_dmData
  //   w_aluC
  //   w_regAddr
  //   w_regData
endmodule

module PC (
  input  in_1,
  input  in_2,
  output out_3
);


  assign out_3 = in_2;
endmodule

module IM (
  input  in_1,
  output out_2
);


  assign out_2 = in_1;
endmodule

module FD (
  input  in_1,
  input  in_2,
  input  in_3,
  output out_4,
  output out_5
);


  assign out_4 = in_2;
  assign out_5 = in_3;
endmodule

module RF (
  input  in_1,
  input  in_2,
  input  in_3,
  input  in_4,
  input  in_5,
  input  in_6,
  output out_7,
  output out_8
);
endmodule

module EXT (
  input  in_1,
  input  in_2,
  output out_3
);
endmodule

module NPC (
  input  in_1,
  input  in_2,
  input  in_3,
  input  in_4,
  input  in_5,
  input  in_6,
  input  in_7,
  output out_8
);
endmodule

module Control (
  input  in_1,
  output out_2,
  output out_3,
  output out_4,
  output out_5,
  output out_6,
  output out_7,
  output out_8,
  output out_9
);
endmodule

module DE (
  input  in_1,
  input  in_2,
  input  in_3,
  input  in_4,
  input  in_5,
  input  in_6,
  input  in_7,
  output out_8,
  output out_9,
  output out_10,
  output out_11,
  output out_12,
  output out_13,
  output out_14
);
endmodule

module ALU (
  input  in_1,
  input  in_2,
  input  in_3,
  output out_4
);
endmodule

module EM (
  input  in_1,
  input  in_2,
  input  in_3,
  input  in_4,
  input  in_5,
  input  in_6,
  output out_7,
  output out_8,
  output out_9,
  output out_10,
  output out_11,
  output out_12,
  output out_13
);
endmodule

module DM (
  input  in_1,
  input  in_2,
  input  in_3,
  input  in_4,
  output out_5
);
endmodule

module MW (
  input  in_1,
  input  in_2,
  input  in_3,
  input  in_4,
  input  in_5,
  output out_6,
  output out_7,
  output out_8,
  output out_9,
  output out_10
);
endmodule

module ADD8 (
  input  in_1,
  output out_2
);
endmodule
