// Logisim project mod5.circ as structural Verilog: 3 circuits, main circuit StateRefresh
module StateRefresh (
  input  [1:0] C,
  input  b,
  output [1:0] NewC
);

  wire and_1_out, and_2_out, and_3_out, and_4_out, and_5_out, and_6_out, not_1_out, not_2_out, not_3_out,
       not_4_out, not_5_out, not_6_out, not_7_out, not_8_out;

  not not_1 (not_1_out, C[0]);
  not not_2 (not_2_out, C[1]);
  not not_3 (not_3_out, C[0]);
  not not_4 (not_4_out, C[1]);
  not not_5 (not_5_out, C[0]);
  not not_6 (not_6_out, b);
  not not_7 (not_7_out, C[1]);
  not not_8 (not_8_out, b);
  and and_1 (and_1_out, not_1_out, C[1]);
  and and_2 (and_2_out, C[0], not_2_out);
  and and_3 (and_3_out, not_3_out, not_4_out, b);
  and and_4 (and_4_out, not_5_out, C[1], not_6_out);
  and and_5 (and_5_out, C[0], not_7_out, not_8_out);
  and and_6 (and_6_out, C[0], C[1], b);
  or or_1 (NewC[0], and_1_out, and_2_out);
  or or_2 (NewC[1], and_3_out, and_4_out, and_5_out, and_6_out);
endmodule

module StateOut (
  input  [1:0] C,
  input  b,
  output S0,
  output S1,
  output S2,
  output S3,
  output S4
);

  wire and_1_out, and_2_out, and_3_out, and_4_out, and_5_out, and_6_out, and_7_out, and_8_out, not_1_out,
       not_2_out, not_3_out, not_4_out, not_5_out, not_6_out, not_7_out, not_8_out, not_9_out, not_10_out,
       not_11_out, not_12_out;

  not not_1 (not_1_out, C[0]);
  not not_2 (not_2_out, C[1]);
  not not_3 (not_3_out, b);
  not not_4 (not_4_out, b);
  not not_5 (not_5_out, C[0]);
  not not_6 (not_6_out, C[1]);
  not not_7 (not_7_out, C[0]);
  not not_8 (not_8_out, C[1]);
  not not_9 (not_9_out, C[0]);
  not not_10 (not_10_out, b);
  not not_11 (not_11_out, C[1]);
  not not_12 (not_12_out, b);
  and and_1 (and_1_out, not_1_out, not_2_out, not_3_out);
  and and_2 (and_2_out, C[0], C[1], not_4_out);
  and and_3 (and_3_out, not_5_out, not_6_out, b);
  and and_4 (and_4_out, C[0], C[1], b);
  and and_5 (and_5_out, not_7_out, C[1], b);
  and and_6 (and_6_out, C[0], not_8_out, b);
  and and_7 (and_7_out, not_9_out, C[1], not_10_out);
  and and_8 (and_8_out, C[0], not_11_out, not_12_out);
  or or_1 (S1, and_1_out, and_2_out);
  or or_2 (S2, and_3_out, and_4_out);
  or or_3 (S3, and_5_out, and_6_out);
  or or_4 (S4, and_7_out, and_8_out);

  assign S0 = 1'b0;
endmodule

module mod5 (
  input  in_1,
  output out_2,
  output out_3,
  output out_4,
  output out_5,
  output out_6
);

  wire clock_1_out;
  wire [1:0] register_1_q, StateRefresh_newc;

  StateRefresh StateRefresh (.C(register_1_q), .b(in_1), .NewC(StateRefresh_newc));
  Clock clock_1 (.out(clock_1_out));
  Register #(.width(2)) register_1 (.D(StateRefresh_newc), .en(1'b1), .Q(register_1_q), .clk(clock_1_out), .clr(1'b0));
  StateOut StateOut (.C(register_1_q), .b(in_1), .S0(out_2), .S1(out_3), .S2(out_4), .S3(out_5), .S4(out_6));
endmodule
