// Logisim project 4bit_sort.circ as structural Verilog: 3 circuits, main circuit 4bit_sort
module _1bit_swap (
  input  l1,
  input  l2,
  input  s,
  output O1,
  output O2
);

  wire and_1_out, and_2_out, and_3_out, and_4_out, not_1_out, not_2_out;

  not not_1 (not_1_out, s);
  not not_2 (not_2_out, s);
  and and_1 (and_1_out, l2, s);
  and and_2 (and_2_out, l1, not_1_out);
  and and_3 (and_3_out, l2, not_2_out);
  and and_4 (and_4_out, l1, s);
  or or_1 (O1, and_1_out, and_2_out);
  or or_2 (O2, and_3_out, and_4_out);
endmodule

module _4bit_swap (
  input  [3:0] l1,
  input  [3:0] l2,
  input  s,
  output [3:0] O1,
  output [3:0] O2
);

  _1bit_swap u_1bit_swap_1 (.l1(l1[0]), .l2(l2[0]), .s(s), .O1(O1[0]), .O2(O2[0]));
  _1bit_swap u_1bit_swap_2 (.l1(l1[1]), .l2(l2[1]), .s(s), .O1(O1[1]), .O2(O2[1]));
  _1bit_swap u_1bit_swap_3 (.l1(l1[2]), .l2(l2[2]), .s(s), .O1(O1[2]), .O2(O2[2]));
  _1bit_swap u_1bit_swap_4 (.l1(l1[3]), .l2(l2[3]), .s(s), .O1(O1[3]), .O2(O2[3]));
endmodule

module _4bit_sort (
  input  [3:0] A,
  input  [3:0] B,
  input  [3:0] C,
  input  [3:0] D,
  output [3:0] _1,
  output [3:0] _2,
  output [3:0] _3,
  output [3:0] _4
);

  wire comparator_1_gt, comparator_2_gt, comparator_3_gt, comparator_4_gt, comparator_5_gt, comparator_6_gt;
  wire [3:0] n4bit_swap_1_o1, n4bit_swap_1_o2, n4bit_swap_2_o1, n4bit_swap_2_o2, n4bit_swap_3_o1,
       n4bit_swap_3_o2, n4bit_swap_4_o1, n4bit_swap_5_o1;

  Comparator #(.width(4), .mode("unsigned")) comparator_1 (.a(A), .b(B), .gt(comparator_1_gt));  // open: eq, lt
  // Probe on comparator_1_gt
  _4bit_swap u_4bit_swap_1 (.l1(A), .l2(B), .s(comparator_1_gt), .O1(n4bit_swap_1_o1), .O2(n4bit_swap_1_o2));
  // Probe on n4bit_swap_1_o2
  // Probe on n4bit_swap_1_o1
  Comparator #(.width(4), .mode("unsigned")) comparator_2 (
    .a(n4bit_swap_1_o2), .b(C), .gt(comparator_2_gt));  // open: eq, lt
  _4bit_swap u_4bit_swap_2 (
    .l1(n4bit_swap_1_o2), .l2(C), .s(comparator_2_gt), .O1(n4bit_swap_2_o1), .O2(n4bit_swap_2_o2));
  Comparator #(.width(4), .mode("unsigned")) comparator_3 (
    .a(n4bit_swap_1_o1), .b(n4bit_swap_2_o1), .gt(comparator_3_gt));  // open: eq, lt
  Comparator #(.width(4), .mode("unsigned")) comparator_4 (
    .a(n4bit_swap_2_o2), .b(D), .gt(comparator_4_gt));  // open: eq, lt
  _4bit_swap u_4bit_swap_3 (
    .l1(n4bit_swap_1_o1), .l2(n4bit_swap_2_o1), .s(comparator_3_gt), .O1(n4bit_swap_3_o1),
    .O2(n4bit_swap_3_o2));
  _4bit_swap u_4bit_swap_4 (.l1(n4bit_swap_2_o2), .l2(D), .s(comparator_4_gt), .O1(n4bit_swap_4_o1), .O2(_4));
  Comparator #(.width(4), .mode("unsigned")) comparator_5 (
    .a(n4bit_swap_3_o2), .b(n4bit_swap_4_o1), .gt(comparator_5_gt));  // open: eq, lt
  _4bit_swap u_4bit_swap_5 (
    .l1(n4bit_swap_3_o2), .l2(n4bit_swap_4_o1), .s(comparator_5_gt), .O1(n4bit_swap_5_o1), .O2(_3));
  Comparator #(.width(4), .mode("unsigned")) comparator_6 (
    .a(n4bit_swap_3_o1), .b(n4bit_swap_5_o1), .gt(comparator_6_gt));  // open: eq, lt
  _4bit_swap u_4bit_swap_6 (.l1(n4bit_swap_3_o1), .l2(n4bit_swap_5_o1), .s(comparator_6_gt), .O1(_1), .O2(_2));

  // Notes on the sheet:
  //   4bit_swap
  //   4bit_swap
  //   4bit_swap
  //   4bit_swap
  //   4bit_swap
  //   4bit_swap
endmodule
