// Logisim project fibonacci.circ as structural Verilog: 1 circuit, main circuit main
module main (
  input  [2:0] \input ,
  input  reset,
  output [3:0] out_3
);

  wire clock_1_out, clock_2_out, continual, continual2, not_1_out;
  wire [3:0] adder_1_out, bit_extender_1_out, counter_1_q;
  wire [7:0] controlled_buffer_1_out, multiplexer_1_out, register_1_q;
  wire [7:4] controlled_buffer_2_out;

  Multiplexer #(.width(8)) multiplexer_1 (
    .in0(controlled_buffer_1_out), .in1(8'h10), .out(multiplexer_1_out), .sel(continual2));  // open: en
  Register register_1 (.D(multiplexer_1_out), .Q(register_1_q), .clk(clock_1_out), .clr(reset));  // open: en
  Clock clock_1 (.out(clock_1_out));
  Counter #(.width(4), .max('hf)) counter_1 (
    .count(continual), .Q(counter_1_q), .clk(clock_2_out), .clr(reset));  // open: load, D, carry
  Clock clock_2 (.out(clock_2_out));
  assign bit_extender_1_out = {{1{1'b0}}, \input };  // Bit_Extender bit_extender_1
  Comparator #(.width(4), .mode("unsigned")) comparator_1 (
    .a(bit_extender_1_out), .b(counter_1_q), .gt(continual));  // open: eq, lt
  Comparator #(.width(4), .mode("unsigned")) comparator_2 (
    .a(counter_1_q), .b(4'b0000), .eq(continual2));  // open: gt, lt
  Adder #(.width(4)) adder_1 (.a(register_1_q[3:0]), .b(register_1_q[7:4]), .out(adder_1_out));  // open: cin, cout
  assign controlled_buffer_1_out = continual ? {adder_1_out, register_1_q[7:4]} : 8'bz;  // Controlled_Buffer controlled_buffer_1
  not not_1 (not_1_out, continual);
  assign {controlled_buffer_2_out, out_3} = not_1_out ? {adder_1_out, register_1_q[7:4]} : 8'bz;  // Controlled_Buffer controlled_buffer_2
endmodule
