// Logisim project sequence.circ as structural Verilog: 2 circuits, main circuit main
module main (
  input  [1:0] in_1,
  input  in_2,
  input  in_3,
  output [31:0] out_4
);

  wire [31:0] multiplexer_1_out, multiplexer_2_out, register_2_q, staterefresh_1_out_4, staterefresh_1_out_5;

  stateRefresh staterefresh_1 (
    .in_1(multiplexer_1_out), .in_2(in_1), .in_3(multiplexer_2_out), .out_4(staterefresh_1_out_4),
    .out_5(staterefresh_1_out_5));
  Register #(.width(32)) register_1 (.D(staterefresh_1_out_4), .Q(out_4), .clk(in_2));  // open: en, clr
  Register #(.width(32)) register_2 (.D(staterefresh_1_out_5), .Q(register_2_q), .clk(in_2));  // open: en, clr
  Multiplexer #(.width(32)) multiplexer_1 (
    .in0(out_4), .in1({32{1'b0}}), .out(multiplexer_1_out), .sel(in_3));  // open: en
  Multiplexer #(.width(32)) multiplexer_2 (
    .in0(register_2_q), .in1({32{1'b0}}), .out(multiplexer_2_out), .sel(in_3));  // open: en

  // Other names for the same wires on the sheet: clk = in_2; reset = in_3
endmodule

module stateRefresh (
  input  [31:0] in_1,
  input  [1:0] in_2,
  input  [31:0] in_3,
  output [31:0] out_4,
  output [31:0] out_5
);

  wire comparator_1_eq, comparator_2_eq, comparator_3_eq;

  Comparator #(.width(2), .mode("unsigned")) comparator_1 (.a(2'b00), .b(in_2), .eq(comparator_1_eq));  // open: gt, lt
  Comparator #(.width(2), .mode("unsigned")) comparator_2 (.a(2'b01), .b(in_2), .eq(comparator_2_eq));  // open: gt, lt
  Comparator #(.width(2), .mode("unsigned")) comparator_3 (.a(2'b10), .b(in_2), .eq(comparator_3_eq));  // open: gt, lt
  assign out_4 = comparator_1_eq ? {32{1'b0}} : 32'bz;  // Controlled_Buffer controlled_buffer_1
  assign out_4 = comparator_2_eq ? in_1 : 32'bz;  // Controlled_Buffer controlled_buffer_2
  assign out_4 = comparator_3_eq ? in_3 : 32'bz;  // Controlled_Buffer controlled_buffer_3
  Adder #(.width(32)) adder_1 (.a(out_4), .b(in_3), .out(out_5));  // open: cin, cout

  // Other names for the same wires on the sheet: n[31:0] = in_1; sum[31:0] = in_3; type[1:0] = in_2
endmodule
